// Logisim project IF.circ as structural Verilog: 3 circuits, main circuit main
module main (
  input  isBranchTaken,
  input  [31:0] in_2,
  input  in_3,
  output [31:0] out_4
);

  wire Clk_out;
  wire [31:0] adder_1_out, multiplexer_1_out, PC_q;

  Register #(.width(32), .trigger("falling")) PC (
    .D(multiplexer_1_out), .en(1'b1), .Q(PC_q), .clk(Clk_out), .clr(in_3));
  Clock Clk (.out(Clk_out));
  Adder #(.width(32)) adder_1 (.a(32'h4), .b(PC_q), .out(adder_1_out));  // open: cin, cout
  ROM #(.addrWidth(24), .dataWidth(32)) rom_1 (.addr(PC_q[25:2]), .data(out_4));  // open: sel
  Multiplexer #(.width(32), .enable("false")) multiplexer_1 (
    .in0(adder_1_out), .in1(in_2), .out(multiplexer_1_out), .sel(isBranchTaken));

  // Notes on the sheet:
  //   contents of rom_1 (hex, n*v repeats v):
  //   54400003 54400024
  //   Instruction
  //   branchPC
endmodule

module of (
  input  [31:0] PC,
  input  [31:0] Inst,
  output [31:0] out_3
);

  wire cu_1_isand, cu_1_isimmediate;
  wire [4:0] adder_1_out;

  Adder #(.width(5)) adder_1 (.a({1'b0, Inst[11:8]}), .b({1'b0, Inst[11:8]}), .out(adder_1_out));  // open: cin, cout
  Shifter #(.width(32), .shift("rr")) shifter_1 (.in({{24{1'b0}}, Inst[7:0]}), .\dist (adder_1_out), .out(out_3));
  CU cu_1 (
    .I_Bit(Inst[25]), .opcode(Inst[24:21]), .isImmediate(cu_1_isimmediate), .isAND(cu_1_isand));  // open: isEOR, isSUB, isRSB, isADD, isADC, isSBC, isRSC, isTST, isTEQ, isCMP, isCMN, isORR, isMOV, isBIC, isMVN
endmodule

// Control Unit
module CU (
  input  I_Bit,
  input  [3:0] opcode,
  output isImmediate,
  output isAND,
  output isEOR,
  output isSUB,
  output isRSB,
  output isADD,
  output isADC,
  output isSBC,
  output isRSC,
  output isTST,
  output isTEQ,
  output isCMP,
  output isCMN,
  output isORR,
  output isMOV,
  output isBIC,
  output isMVN
);

  Decoder #(.select(4), .enable("false")) decoder_1 (
    .out0(isAND), .out1(isEOR), .out2(isSUB), .out3(isRSB), .out4(isADD), .out5(isADC), .out6(isSBC),
    .out7(isRSC), .out8(isTST), .out9(isTEQ), .out10(isCMP), .out11(isCMN), .out12(isORR), .out13(isMOV),
    .out14(isBIC), .out15(isMVN), .sel(opcode));

  assign isImmediate = I_Bit;
endmodule
